# Fritzing sketch Ligações (saved by Fritzing 0.9.3b)
breadboards: 1

parts:
  Componente1 = Arduino Uno (Rev3)
  U1 = 7-SEGMENT-DISPLAY-1_-RED [package=7-segment-1_pth]
  LED2 = smd LED [color="Green (565nm)" package="1206 [SMD]"]
  R1 = Resistor [tolerance=±5% resistance=330 package="2010 [SMD]"]
  R3 = Resistor [tolerance=±5% resistance=330 package="2010 [SMD]"]
  S1 = Pushbutton [package="[THT]"]
  S2 = Pushbutton [package="[THT]"]
  R4 = Resistor [tolerance=±5% resistance=330 package="2010 [SMD]"]
  R5 = Resistor [tolerance=±5% resistance=330 package="2010 [SMD]"]
  SG1 = Buzzer 12mm [package=buzzer-12mm-ns]

nets:
  N1: Componente1.D8, U1.D
  N2: Componente1.D9_PWM, U1.E
  N3: Componente1.D10_PWM/SS, U1.B
  N4: Componente1.D11_PWM/MOSI, U1.A
  N5: Componente1.D12/MISO, U1.F
  N6: Componente1.D13/SCK, U1.G
  N7: Componente1.D2, LED2.anode
  N8: Componente1.D3_PWM, SG1.2
  N9: Componente1.D4, S1.Pin_1, S1.Pin_2, R5.Pin_0
  N10: Componente1.D5_PWM, S2.Pin_1, S2.Pin_2, R4.Pin_0
  N11: Componente1.D6_PWM, U1.DP
  N12: Componente1.D7, U1.C
  N13: Componente1.5V, S1.Pin_3, S1.Pin_4, S2.Pin_3, S2.Pin_4
  N14: Componente1.GND, R1.Pin_1, R3.Pin_1, R4.Pin_1, R5.Pin_1, SG1.1
  N15: U1.G1, R3.Pin_0
  N16: LED2.cathode, R1.Pin_0
